# Fritzing sketch data-logger-layout (saved by Fritzing 0.9.3b)

parts:
  Part1 = Arduino Uno (Rev3)
  Part4 = Adafruit BME280
  microSD1 = MicroSD Breakout
  Part5 = Soil Moisture Sensor

nets:
  N1: Part1.A0, Part5.SIG
  N2: Part1.A4/SDA, Part4.SDI/SDA
  N3: Part1.A5/SCL, Part4.CS
  N4: Part1.D10_PWM/SS, microSD1.CS
  N5: Part1.D11_PWM/MOSI, microSD1.DI
  N6: Part1.D12/MISO, microSD1.DO
  N7: Part1.D13/SCK, microSD1.CLK
  5V: Part1.5V, Part4.VIN, microSD1.5V, Part5.VCC
  GND: Part1.GND, Part4.GND, microSD1.GND, Part5.GND

custom parts:
  Adafruit BME280: Bosch has stepped up their game with their new BME280 sensor, an environmental sensor with temperature, barometric pressure and humidity! This sensor is great for all sorts of weather/environmental sensing and can even be used in both I2C and SPI! This precision sensor from Bosch is the best low-cost sensing solution for measuring humidity with ±3% accuracy, barometric pressure with ±1 hPa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
  MicroSD Breakout: 5V-ready microSD Breakout with Level Shifter
